// Logisim project part 2 with 7400 gates.circ as structural Verilog: 1 circuit, main circuit main
module main (
  input  a,
  input  b,
  input  c,
  input  d
);

  wire n7404_1_p2, n7404_1_p4, n7404_1_p6, n7408_1_p3, n7408_1_p6, n7432_1_p3;

  // _7404 7404_1: pin names not known; wires that end beside it: a, n7404_1_p2, b, n7404_1_p4, c, n7404_1_p6
  // _7408 7408_1: pin names not known; wires that end beside it: n7404_1_p2, n7404_1_p6, n7408_1_p3, n7404_1_p4, d, n7408_1_p6
  // _7432 7432_1: pin names not known; wires that end beside it: n7408_1_p3, n7408_1_p6, n7432_1_p3
  LED led_1 (.in(n7432_1_p3));
endmodule
